# Fritzing sketch circuit-diagram-sketch (saved by Fritzing 0.9.9b)
breadboards: 1

parts:
  Part1 = Arduino Uno (Rev3)
  Mod1 = Raspberry Pi 4B  # not connected
  S3 = Pushbutton [package="[SMD]"]
  SPKR1 = Loudspeaker
  R4 = Rotary Potentiometer (Small) [maximum_resistance=100kΩ package=THT]
  R6 = Resistor [tolerance=±5% power=0.25 resistance=10k package=THT]
  R2 = Basic Flex Resistor
  R7 = Resistor [tolerance=±5% power=0.25 resistance=10k package=THT]
  Part2 = Breakout Board for Electret Microphone
  U1 = TCM8240MD [package=tcm8240md]  # not connected

nets:
  N1: Part1.A0, R4.wiper
  N2: Part1.A1, R2.Pin_2, R7.Pin_1
  N3: Part1.A2, Part2.AUD
  N4: Part1.D8, SPKR1.pin1
  GND: Part1.GND, S3.Pin_3, S3.Pin_4, R4.leg2, R2.pin_1, Part2.GND
  N5: Part1.D2, S3.Pin_1, S3.Pin_2, R6.Pin_0
  5V: Part1.5V, SPKR1.pin2, R4.leg1, R6.Pin_1, R7.Pin_0, Part2.VCC
